// Logisim project alu.circ as structural Verilog: 1 circuit, main circuit main
module main (
  input  [15:0] X,
  input  [15:0] Y,
  input  [2:0] Switch,
  output Equal,
  output [15:0] Result,
  output [15:0] Result_2
);

  wire lt_1;
  wire [15:0] add, \and , lt, mult, \or , sll, srl, \xor ;

  Shifter #(.width(16)) shifter_1 (.in(X), .\dist (Y[3:0]), .out(sll));
  Shifter #(.width(16), .shift("lr")) shifter_2 (.in(X), .\dist (Y[3:0]), .out(srl));
  Adder #(.width(16)) adder_1 (.a(X), .b(Y), .out(add));  // open: cin, cout
  assign \and  = X & Y;  // AND_Gate and_1, 16 bits wide
  assign \or  = X | Y;  // OR_Gate or_1, 16 bits wide
  assign \xor  = X ^ Y;  // XOR_Gate xor_1, 16 bits wide
  Comparator #(.width(16)) comparator_1 (.a(X), .b(Y), .eq(Equal), .lt(lt_1));  // open: gt
  Multiplier #(.width(16)) multiplier_1 (.a(X), .b(Y), .out(mult), .cout(Result_2));  // open: cin
  assign lt = {{15{1'b0}}, lt_1};  // Bit_Extender bit_extender_1
  Multiplexer #(.select(3), .width(16)) multiplexer_1 (
    .in0(sll), .in1(srl), .in2(add), .in3(\and ), .in4(\or ), .in5(\xor ), .in6(lt), .in7(mult),
    .out(Result), .sel(Switch));  // open: en

  // Other names for the same wires on the sheet: S[2:0] = Switch; Y_4[3:0] = Y[3:0]

  // Notes on the sheet:
  //   INPUTS to your circuit
  //   DON'T CHANGE THE LOCATIONS OF THE INPUTS AND OUTPUTS!
  //   OUTPUTS from your circuit
endmodule
